# Fritzing sketch MycoFarmMarthaV1 (saved by Fritzing 0.9.5d)
circuit board: 6.88566cm x 5.36311cm

parts:
  Arduino = Arduino Uno (Rev3) - ICSP
  DHT/CCS = RJ45 Jack [package=rj45-8]

nets:
  N1: Arduino.A4/SDA, DHT/CCS.4
  N2: Arduino.A5/SCL, DHT/CCS.2
  N3: Arduino.5V, DHT/CCS.3, DHT/CCS.8
  N4: Arduino.GND, DHT/CCS.1, DHT/CCS.5, DHT/CCS.6
  N5: Arduino.D8, DHT/CCS.7

notes:
  1: CCS811 GND
  4: CCS811 SDA
  3: CCS811 VIN
  2: CCS811 SCL
  5: CCS811 WAKE
  6: DHT22 GND
  7: DHT22 DATA
  8: DHT22 VIN
