# Fritzing sketch MycoFarmV1 (saved by Fritzing 0.9.5d)
breadboards: 2

parts:
  Part1 = Arduino Uno (Rev3) - ICSP
  DHT1 = DHT11 Humitidy and Temperature Sensor
  Part2 = Adafruit CCS811
  U1 = 4RelayModule
  Raspberry_Pi_1 = Raspberry Pi 3 [part_number=RPI-3-V1.2]  # not connected
  Q1 = PNP-Transistor [part_number=2N3906 package="TO92 [THT]"]
  Q2 = NPN-Transistor [part_number=2N3904 package="TO92 [THT]"]
  R1 = Resistor [tolerance=±5% resistance=1k package="2512 [SMD]"]
  12VDC = 2.1mm Barrel Jack with Terminal Block
  5VDC2 = 2.1mm Barrel Jack with Terminal Block
  5VDC1 = 2.1mm Barrel Jack with Terminal Block  # not connected
  24VAC = 2.1mm Barrel Jack with Terminal Block
  24VAC_Irrigation_Solenoid = Solenoid
  R2 = Resistor [tolerance=±5% resistance=1k package="2512 [SMD]"]
  o1 = Module display OLED I2C 128x64 SSD1306 [package=THT]
  Pad_Heater_?VDC = Peltier Element  # not connected
  Grow_Lamp_5VDC = LEDs [package=led10mm]  # not connected
  12V_FAE_Case_Fan = Fan - Ventilador [package=THT]
  D1 = Diode [package=diode-1n4001]
  D2 = Diode [package=diode-1n4001]
  D3 = Diode [package=diode-1n4001]
  D4 = Diode [package=diode-1n4001]
  Part4 = Arduino Prototyping Shield
  J1 = COMPUTER-PERIPHERAL-POWER [package=computer-peripheral-power-ra]
  J2 = male pin header, 2 pins [form="♂ (male)"]
  J3 = male pin header, 2 pins [form="♂ (male)"]  # not connected
  J4 = male pin header, 2 pins [form="♂ (male)"]
  12V_FAE_Case_Fan1 = Fan - Ventilador [package=THT]
  Part5 = Arduino Uno (Rev3) - ICSP  # not connected
  R3 = Resistor [tolerance=±5% resistance=1k package="2512 [SMD]"]
  R4 = Resistor [tolerance=±5% resistance=1k package="2512 [SMD]"]
  J5 = male pin header, 2 pins [form="♂ (male)"]
  Q5 = PNP-Transistor [part_number=2N3906 package="TO92 [THT]"]
  U2 = 4RelayModule
  J7 = male pin header, 4 pins [form="♂ (male)"]
  J6 = male pin header, 8 pins [form="♂ (male)"]
  DHT2 = DHT11 Humitidy and Temperature Sensor
  Part6 = Adafruit CCS811
  o2 = Module display OLED I2C 128x64 SSD1306 [package=THT]
  D5 = Diode [package=diode-1n4001]
  D6 = Diode [package=diode-1n4001]
  D7 = Diode [package=diode-1n4001]
  D8 = Diode [package=diode-1n4001]
  Q6 = NPN-Transistor [part_number=2N3904 package="TO92 [THT]"]
  J8 = male pin header, 6 pins [form="♂ (male)"]
  J9 = male pin header, 2 pins [form="♂ (male)"]
  J10 = male pin header, 2 pins [form="♂ (male)"]
  Part7 = Arduino Nano (Rev3.0) (ICSP)
  Part8 = OLED Monochrome 128x64 1.3 inch [part_number=938]
  Part9 = Arduino Nano (Rev3.0) (ICSP)
  Part10 = Adafruit CCS811
  DHT3 = DHT11 Humitidy and Temperature Sensor
  7-12VDC = 2.1mm Barrel Jack with Terminal Block
  Raspberry_Pi_2 = Raspberry Pi 3 [part_number=RPI-3-V1.2]  # not connected
  5VDC = 2.1mm Barrel Jack with Terminal Block  # not connected

nets:
  N1: Part1.D8, DHT1.VDD
  N2: Part1.D9_PWM, D4.A
  N3: Part1.D10_PWM/SS, D3.A
  N4: Part1.D11_PWM/MOSI, D2.A
  N5: Part1.D12/MISO, D1.A
  N6: Part1.D6_PWM, R2.Pin_1
  VIN: DHT1.DATA, Part2.VIN, 5VDC2.POS, o1.VCC, Part7.5V
  GND: DHT1.NULL, Part2.GND, Part2.!WAKE, U1.GND, Q2.E, 12VDC.NEG, 5VDC2.NEG, o1.GND, 12V_FAE_Case_Fan.GND, Part7.GND
  N7: Part2.SDA, o1.SDA, Part7.A4
  N8: Part2.SCL, o1.SCL, Part7.A5
  N9: U1.IN2, D2.C
  N10: U1.NC1, 24VAC.POS
  N11: U1.NO1, 24VAC_Irrigation_Solenoid.pin2
  N12: U1.IN1, D1.C
  N13: U1.VCC, Q1.E, 12VDC.POS
  N14: U1.IN3, D3.C
  N15: U1.IN4, D4.C
  N16: Q1.B, R1.Pin_0
  N17: Q1.C, 12V_FAE_Case_Fan.5V
  N18: Q2.B, R2.Pin_0
  N19: Q2.C, R1.Pin_1
  N20: 24VAC.NEG, 24VAC_Irrigation_Solenoid.pin1
  N21: Part4.D6, R3.Pin_1
  N22: Part4.D9, D8.A
  N23: Part4.D10, D7.A
  N24: Part4.D11, D6.A
  N25: Part4.D12, D5.A
  GND_2: Part4.GND, Part4.N$33, Part4.N$34, Part4.N$41, Part4.N$42, Part4.N$44, Part4.N$65, Part4.N$68, Part4.N$89, Part4.N$240, J1.GND, J1.NC, J2.pin1, J5.pin1, U2.IN2, Q6.E, J8.pin4, J10.pin1
  N26: Part4.N$29, Part4.N$84, Part4.N$86, Part4.N$90, Part4.N$233, J1.5V, J4.pin1
  N27: Part4.N$78, J4.pin2
  N28: Part4.N$117, J6.pin1, Part6.!WAKE
  N29: Part4.N$167, Part4.N$179, U2.IN4, D6.C, J8.pin2
  N30: Part4.N$168, Part4.N$180, U2.IN3, D5.C, J8.pin3
  N31: Part4.N$227, Part4.N$229, U2.VCC, D7.C, J8.pin1
  N32: Part4.N$228, Part4.N$230, D8.C
  N33: Part4.N$267, Part4.N$311, R4.Pin_0, Q6.C
  N34: Part4.N$294, Part4.N$295, R4.Pin_1, Q5.B
  N35: Part4.N$307, Part4.N$420, R3.Pin_0, Q6.B
  N36: Part4.N$316, Part4.N$380, Q5.C
  N37: Part4.N$321, J7.pin4, o2.SDA
  N38: Part4.N$322, J7.pin3, o2.SCL
  N39: Part4.N$324, J7.pin2, o2.VCC
  GND_3: Part4.N$325, Part4.N$326, 12V_FAE_Case_Fan1.GND, J7.pin1, o2.GND, J9.pin2
  N40: Part4.N$329, Part4.N$331, Part4.N$332, J1.12V, J2.pin2, J5.pin2, J10.pin2
  N41: Part4.N$353, 12V_FAE_Case_Fan1.5V, J9.pin1
  N42: Part4.N$376, Q5.E
  N43: Part4.N$393, J6.pin2, Part6.SCL
  N44: Part4.N$396, J6.pin3, Part6.SDA
  N45: Part4.N$398, J6.pin4, Part6.GND
  N46: Part4.N$403, J6.pin5, Part6.VIN
  N47: Part4.N$405, J6.pin6, DHT2.NULL
  N48: Part4.N$425, J6.pin7, DHT2.DATA
  N49: Part4.N$427, J6.pin8, DHT2.VDD
  N50: U2.IN1, J8.pin5
  N51: U2.GND, J8.pin6
  N52: Part8.MOSI_SDA, Part9.D11/MOSI
  N53: Part8.SCLK_SCK, Part9.D13/SCK
  N54: Part8.DC_SA0, Part9.D9
  N55: Part8.CS, Part9.D10
  GND_4: Part9.GND, DHT3.GND, 7-12VDC.NEG
  N56: Part9.D7, Part10.!RESET
  N57: Part9.D8, DHT3.DATA
  N58: Part9.VIN, 7-12VDC.POS
  5V: Part9.5V, Part10.VIN, DHT3.VDD
  N59: Part9.A5, Part10.SCL
  N60: Part9.A4, Part10.SDA

notes:
  Per Tub
  Master Controller
  DHT11/22 T&H Sensor
  CCS811 eCO2 Sensor
  USB
  I2C OLED

custom parts:
  DHT11 Humitidy and Temperature Sensor: DHT11 Humidity and Temperature Sensor
  4RelayModule: 4 relay arduino module SONGLE SRD05VDC-SL-C
  Module display OLED I2C 128x64 SSD1306: Ecran OLED I2C SSD163 de 128x64 avec connexion I2C
  Fan - Ventilador: Ventilador de 2 pines, se encuentra comunmente en computadoras de escritorio
  OLED Monochrome 128x64 1.3 inch: These displays are small, only about 1.3" diagonal, but very readable due to the high contrast of an OLED display. This display is made of 128x64 individual white OLED pixels, each one is turned on or off by the controller chip. Because the display makes its own light, no backlight is required. This reduces the power required to run the OLED and is why the display has such high contrast; we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
