# Fritzing sketch TripleStirrerV1 (saved by Fritzing 0.9.5d)
stripboards: 1

parts:
  F1 = Fan - Ventilador [package=THT]
  F2 = Fan - Ventilador [package=THT]
  F3 = Fan - Ventilador [package=THT]
  12VDC = 2.1mm Barrel Jack with Terminal Block
  Q1 = PNP-Transistor [part_number=2N3906 package="TO92 [THT]"]
  Q2 = PNP-Transistor [part_number=2N3906 package="TO92 [THT]"]
  Q3 = PNP-Transistor [part_number=2N3906 package="TO92 [THT]"]
  Q4 = NPN-Transistor [part_number=2N3904 package="TO92 [THT]"]
  Q5 = NPN-Transistor [part_number=2N3904 package="TO92 [THT]"]
  Q6 = NPN-Transistor [part_number=2N3904 package="TO92 [THT]"]
  R6 = Resistor [tolerance=±5% resistance=1k package=THT]
  Part1 = Arduino Board Ethernet
  part = 2.1mm Barrel Jack with Terminal Block
  BUTTON1 = Waterproof Pushbutton (red)
  BUTTON2 = Waterproof Pushbutton (red)
  BUTTON3 = Waterproof Pushbutton (red)
  J1 = female pin header, 4 pins [form="♀ (female)"]
  J3 = female pin header, 4 pins [form="♀ (female)"]
  J2 = female pin header, 7 pins [form="♀ (female)"]
  R7 = Resistor [tolerance=±5% resistance=1k package=THT]
  R8 = Resistor [tolerance=±5% resistance=1k package=THT]
  R9 = Resistor [tolerance=±5% resistance=1k package=THT]
  R10 = Resistor [tolerance=±5% resistance=1k package=THT]
  R11 = Resistor [tolerance=±5% resistance=1k package=THT]

nets:
  N1: F1.5V, Q3.B, J1.pin1
  GND: F1.GND, F2.GND, F3.GND
  N2: F2.5V, Q2.B, J1.pin2
  N3: F3.5V, Q1.B, J1.pin3
  N4: 12VDC.POS, Q1.C, Q2.C, Q3.C, part.POS
  N5: 12VDC.NEG, Q4.E, Q5.E, Q6.E, Part1.GND, part.NEG, BUTTON1.no_name_yet#1, BUTTON1.no_name_yet#5, BUTTON2.no_name_yet#1, BUTTON2.no_name_yet#5, BUTTON3.no_name_yet#1, BUTTON3.no_name_yet#5, J1.pin4, J3.pin4, J2.pin7
  N6: Q1.E, R6.Pin_1
  N7: Q2.E, R7.Pin_1
  N8: Q3.E, R8.Pin_1
  N9: Q4.B, R11.Pin_1
  N10: Q4.C, R6.Pin_0
  N11: Q5.B, R9.Pin_1
  N12: Q5.C, R8.Pin_0
  N13: Q6.B, R10.Pin_1
  N14: Q6.C, R7.Pin_0
  N15: Part1.D8, BUTTON1.no_name_yet#2, J3.pin1
  N16: Part1.A3, BUTTON2.no_name_yet#4, J2.pin4
  N17: Part1.A4, BUTTON3.no_name_yet#4, J2.pin5
  N18: Part1.A5, BUTTON1.no_name_yet#4, J2.pin6
  N19: Part1.D2_PWM, BUTTON2.no_name_yet#2, J3.pin3
  N20: Part1.D3_PWM, R11.Pin_0
  N21: Part1.D5_PWM, R10.Pin_0
  N22: Part1.D6_PWM, R9.Pin_0
  N23: Part1.D7, BUTTON3.no_name_yet#2, J3.pin2

custom parts:
  Fan - Ventilador: Ventilador de 2 pines, se encuentra comunmente en computadoras de escritorio
  Waterproof Pushbutton (red): Waterproof Illuminated Pushbutton (red)
